// Logisim project subleq_64k.circ as structural Verilog: 6 circuits, main circuit main
module main (
);

  wire alu_1_nld_pc, button_1_out, clock_1_out, control_1_ninc_pc, control_1_nld_a, control_1_nld_b,
       control_1_nld_mar_h, control_1_nld_mar_l, control_1_nld_pc_cond, control_1_nsel_addr_pc_mar,
       control_1_nwr_mem, not_1_out, not_2_out, not_3_out, not_4_out, not_5_out, not_6_out, not_7_out,
       not_8_out, not_9_out;
  wire [3:0] memory_1_mem_addr, memory_1_mem_addr_2, memory_1_mem_addr_3, pc_1_pc_q_2, pc_1_pc_q_3,
       registers_1_b, registers_1_b_2;
  wire [7:0] alu_1_mem_dq, pc_1_pc_q, registers_1_a;
  wire [15:0] registers_1_mar;
  wire [15:12] memory_1_mem_addr_4;

  Clock clock_1 (.out(clock_1_out));
  Button button_1 (.out(button_1_out));
  LED CLK (.in(clock_1_out));
  not not_1 (not_1_out, button_1_out);
  LED INC_PC (.in(not_2_out));
  not not_2 (not_2_out, control_1_ninc_pc);
  not not_3 (not_3_out, control_1_nld_mar_h);
  LED LD_MAR_H (.in(not_3_out));
  not not_4 (not_4_out, control_1_nsel_addr_pc_mar);
  LED SEL_ADDR_PC_MAR (.in(not_4_out));
  LED LD_MAR_L (.in(not_5_out));
  not not_5 (not_5_out, control_1_nld_mar_l);
  not not_6 (not_6_out, control_1_nld_pc_cond);
  LED LD_PC_COND (.in(not_6_out));
  not not_7 (not_7_out, control_1_nwr_mem);
  LED WR_MEM (.in(not_7_out));
  LED LD_B (.in(not_8_out));
  not not_8 (not_8_out, control_1_nld_b);
  LED LD_A (.in(not_9_out));
  not not_9 (not_9_out, control_1_nld_a);
  registers registers_1 (
    .MEM_DQ(alu_1_mem_dq), .CLK(clock_1_out), .nLD_A(control_1_nld_a), .nLD_B(control_1_nld_b),
    .nLD_MAR_L(control_1_nld_mar_l), .nLD_MAR_H(control_1_nld_mar_h), .A(registers_1_a),
    .B({registers_1_b_2, registers_1_b}), .MAR(registers_1_mar));
  Hex_Digit_Display hex_digit_display_1 (.value(registers_1_a[7:4]));  // open: dp
  Hex_Digit_Display hex_digit_display_2 (.value(registers_1_a[3:0]));  // open: dp
  Hex_Digit_Display hex_digit_display_3 (.value(registers_1_b_2));  // open: dp
  Hex_Digit_Display hex_digit_display_4 (.value(registers_1_b));  // open: dp
  control control_1 (
    .nINC_PC(control_1_ninc_pc), .nLD_MAR_H(control_1_nld_mar_h),
    .nSEL_ADDR_PC_MAR(control_1_nsel_addr_pc_mar), .nLD_MAR_L(control_1_nld_mar_l),
    .nLD_PC_COND(control_1_nld_pc_cond), .nWR_MEM(control_1_nwr_mem), .nLD_B(control_1_nld_b),
    .nLD_A(control_1_nld_a), .nRST(not_1_out), .CLK(clock_1_out));
  Hex_Digit_Display hex_digit_display_5 (.value(registers_1_mar[11:8]));  // open: dp
  Hex_Digit_Display hex_digit_display_6 (.value(registers_1_mar[15:12]));  // open: dp
  Hex_Digit_Display hex_digit_display_7 (.value(registers_1_mar[7:4]));  // open: dp
  Hex_Digit_Display hex_digit_display_8 (.value(registers_1_mar[3:0]));  // open: dp
  pc pc_1 (
    .nCLR(not_1_out), .CLK(clock_1_out), .MAR_Q(registers_1_mar), .nINC_PC(control_1_ninc_pc),
    .nLD_PC(alu_1_nld_pc), .PC_Q({pc_1_pc_q_3, pc_1_pc_q_2, pc_1_pc_q}));
  alu alu_1 (
    .B({registers_1_b_2, registers_1_b}), .A(registers_1_a), .nWR_MEM(control_1_nwr_mem),
    .nLD_PC_COND(control_1_nld_pc_cond), .MEM_DQ(alu_1_mem_dq), .nLD_PC(alu_1_nld_pc));
  Hex_Digit_Display hex_digit_display_9 (.value(pc_1_pc_q_2));  // open: dp
  Hex_Digit_Display hex_digit_display_10 (.value(pc_1_pc_q_3));  // open: dp
  memory memory_1 (
    .MAR_Q(registers_1_mar), .PC_Q({pc_1_pc_q_3, pc_1_pc_q_2, pc_1_pc_q}), .nADDR_OE(1'b0),
    .nSEL_ADD_PC_MAR(control_1_nsel_addr_pc_mar), .nWR_MEM(control_1_nwr_mem),
    .MEM_ADDR({memory_1_mem_addr_4, memory_1_mem_addr_3, memory_1_mem_addr_2, memory_1_mem_addr}),
    .MEM_Q(alu_1_mem_dq), .MEM_D(alu_1_mem_dq));
  Hex_Digit_Display hex_digit_display_11 (.value(pc_1_pc_q[7:4]));  // open: dp
  Hex_Digit_Display hex_digit_display_12 (.value(pc_1_pc_q[3:0]));  // open: dp
  Hex_Digit_Display hex_digit_display_13 (.value(alu_1_mem_dq[3:0]));  // open: dp
  Hex_Digit_Display hex_digit_display_14 (.value(alu_1_mem_dq[7:4]));  // open: dp
  Hex_Digit_Display hex_digit_display_15 (.value(memory_1_mem_addr_3));  // open: dp
  Hex_Digit_Display hex_digit_display_16 (.value(memory_1_mem_addr_4));  // open: dp
  Hex_Digit_Display hex_digit_display_17 (.value(memory_1_mem_addr));  // open: dp
  Hex_Digit_Display hex_digit_display_18 (.value(memory_1_mem_addr_2));  // open: dp

  // Notes on the sheet:
  //   A
  //   B
  //   MAR
  //   PC
  //   MEM_DQ
  //   MEM_ADDR
endmodule

// CONTROL
module control (
  input  nRST,
  input  CLK,
  output nLD_A,
  output nLD_B,
  output nWR_MEM,
  output nLD_PC_COND,
  output nLD_MAR_L,
  output nLD_MAR_H,
  output nSEL_ADDR_PC_MAR,
  output nINC_PC
);

  wire dip_7411_1_y1, dip_7411_1_y2, dip_74107_1_q1, dip_74107_1_q2, dip_74107_1_r1, dip_74107_1_r2,
       dip_74107_2_q1, dip_74107_2_q2, dip_74107_2_r2, dip_74107_3_q1, dip_74107_3_q2, dip_74107_3_r1,
       dip_74107_4_q1, dip_74107_4_q2, dip_74107_4_r2, dip_74107_5_q1, dip_74107_5_q2, dip_74107_5_r1,
       not_1_out;

  DIP_7411 dip_7411_1 (
    .A1(dip_74107_1_q1), .B1(dip_74107_1_r2), .C1(dip_74107_2_r2), .A2(dip_74107_3_r1), .B2(dip_74107_4_r2),
    .C2(dip_74107_5_r1), .A3(dip_7411_1_y2), .B3(1'b1), .C3(dip_7411_1_y1), .Y1(dip_7411_1_y1),
    .Y2(dip_7411_1_y2), .Y3(nINC_PC));
  DIP_7411 dip_7411_2 (
    .A1(dip_74107_1_q1), .B1(dip_74107_2_r2), .C1(dip_74107_4_r2), .A2(dip_74107_1_r2), .B2(dip_74107_3_r1),
    .C2(dip_74107_5_r1), .A3(nWR_MEM), .B3(nLD_B), .C3(nLD_A), .Y1(nLD_MAR_L), .Y2(nLD_MAR_H),
    .Y3(nSEL_ADDR_PC_MAR));
  DIP_74107 dip_74107_1 (
    .J1(nLD_PC_COND), .CLK1(not_1_out), .K1(dip_74107_5_q2), .CLR1(nRST), .J2(dip_74107_1_r1),
    .CLK2(not_1_out), .K2(dip_74107_1_q1), .CLR2(nRST), .Q1(dip_74107_1_q1), .R1(dip_74107_1_r1),
    .Q2(dip_74107_1_q2), .R2(dip_74107_1_r2));
  DIP_74107 dip_74107_2 (
    .J1(dip_74107_1_q2), .CLK1(not_1_out), .K1(dip_74107_1_r2), .CLR1(nRST), .J2(dip_74107_2_q1),
    .CLK2(not_1_out), .K2(nLD_A), .CLR2(nRST), .Q1(dip_74107_2_q1), .R1(nLD_A), .Q2(dip_74107_2_q2),
    .R2(dip_74107_2_r2));
  DIP_74107 dip_74107_3 (
    .J1(dip_74107_2_q2), .CLK1(not_1_out), .K1(dip_74107_2_r2), .CLR1(nRST), .J2(dip_74107_3_q1),
    .CLK2(not_1_out), .K2(dip_74107_3_r1), .CLR2(nRST), .Q1(dip_74107_3_q1), .R1(dip_74107_3_r1),
    .Q2(dip_74107_3_q2), .R2(nLD_B));
  DIP_74107 dip_74107_4 (
    .J1(dip_74107_3_q2), .CLK1(not_1_out), .K1(nLD_B), .CLR1(nRST), .J2(dip_74107_4_q1), .CLK2(not_1_out),
    .K2(nWR_MEM), .CLR2(nRST), .Q1(dip_74107_4_q1), .R1(nWR_MEM), .Q2(dip_74107_4_q2), .R2(dip_74107_4_r2));
  DIP_74107 dip_74107_5 (
    .J1(dip_74107_4_q2), .CLK1(not_1_out), .K1(dip_74107_4_r2), .CLR1(nRST), .J2(dip_74107_5_q1),
    .CLK2(not_1_out), .K2(dip_74107_5_r1), .CLR2(nRST), .Q1(dip_74107_5_q1), .R1(dip_74107_5_r1),
    .Q2(dip_74107_5_q2), .R2(nLD_PC_COND));
  not not_1 (not_1_out, CLK);

  // Notes on the sheet:
  //   ~T0
  //   ~T1
  //   ~T2
  //   ~T3
  //   ~T4
  //   ~T5
  //   ~T6
  //   ~T7
  //   ~T8
  //   ~T9
endmodule

// PC
module pc (
  input  nCLR,
  input  nINC_PC,
  input  CLK,
  input  nLD_PC,
  input  [15:0] MAR_Q,
  output [15:0] PC_Q
);

  wire dip_74161_1_tc, dip_74161_2_tc, dip_74161_3_tc, not_1_out;

  Hex_Digit_Display hex_digit_display_1 (.value(MAR_Q[15:12]));  // open: dp
  Hex_Digit_Display hex_digit_display_2 (.value(MAR_Q[11:8]));  // open: dp
  Hex_Digit_Display hex_digit_display_3 (.value(MAR_Q[3:0]));  // open: dp
  Hex_Digit_Display hex_digit_display_4 (.value(MAR_Q[7:4]));  // open: dp
  DIP_74161 dip_74161_1 (
    .CLK(CLK), .CLR(nCLR), .LE(nLD_PC), .CEP(not_1_out), .CET(not_1_out), .D1(MAR_Q[0]), .D2(MAR_Q[1]),
    .D3(MAR_Q[2]), .D4(MAR_Q[3]), .Q1(PC_Q[0]), .Q2(PC_Q[1]), .Q3(PC_Q[2]), .Q4(PC_Q[3]), .TC(dip_74161_1_tc));
  DIP_74161 dip_74161_2 (
    .CLK(CLK), .CLR(nCLR), .LE(nLD_PC), .CEP(not_1_out), .CET(dip_74161_1_tc), .D1(MAR_Q[4]), .D2(MAR_Q[5]),
    .D3(MAR_Q[6]), .D4(MAR_Q[7]), .Q1(PC_Q[4]), .Q2(PC_Q[5]), .Q3(PC_Q[6]), .Q4(PC_Q[7]), .TC(dip_74161_2_tc));
  DIP_74161 dip_74161_3 (
    .CLK(CLK), .CLR(nCLR), .LE(nLD_PC), .CEP(not_1_out), .CET(dip_74161_2_tc), .D1(MAR_Q[8]), .D2(MAR_Q[9]),
    .D3(MAR_Q[10]), .D4(MAR_Q[11]), .Q1(PC_Q[8]), .Q2(PC_Q[9]), .Q3(PC_Q[10]), .Q4(PC_Q[11]),
    .TC(dip_74161_3_tc));
  DIP_74161 dip_74161_4 (
    .CLK(CLK), .CLR(nCLR), .LE(nLD_PC), .CEP(not_1_out), .CET(dip_74161_3_tc), .D1(MAR_Q[12]),
    .D2(MAR_Q[13]), .D3(MAR_Q[14]), .D4(MAR_Q[15]), .Q1(PC_Q[12]), .Q2(PC_Q[13]), .Q3(PC_Q[14]), .Q4(PC_Q[15]));  // open: TC
  not not_1 (not_1_out, nINC_PC);
  Hex_Digit_Display hex_digit_display_5 (.value(PC_Q[15:12]));  // open: dp
  Hex_Digit_Display hex_digit_display_6 (.value(PC_Q[7:4]));  // open: dp
  Hex_Digit_Display hex_digit_display_7 (.value(PC_Q[11:8]));  // open: dp
  Hex_Digit_Display hex_digit_display_8 (.value(PC_Q[3:0]));  // open: dp
endmodule

// REGS
module registers (
  input  [7:0] MEM_DQ,
  input  CLK,
  input  nLD_A,
  input  nLD_B,
  input  nLD_MAR_L,
  input  nLD_MAR_H,
  output [7:0] A,
  output [7:0] B,
  output [15:0] MAR
);

  Hex_Digit_Display hex_digit_display_1 (.value(MEM_DQ[7:4]));  // open: dp
  Hex_Digit_Display hex_digit_display_2 (.value(MEM_DQ[3:0]));  // open: dp
  DIP_74377 u_A (
    .CE(nLD_A), .CLK(CLK), .D1(MEM_DQ[0]), .D2(MEM_DQ[1]), .D3(MEM_DQ[2]), .D4(MEM_DQ[3]), .D5(MEM_DQ[4]),
    .D6(MEM_DQ[5]), .D7(MEM_DQ[6]), .D8(MEM_DQ[7]), .Q1(A[0]), .Q2(A[1]), .Q3(A[2]), .Q4(A[3]), .Q5(A[4]),
    .Q6(A[5]), .Q7(A[6]), .Q8(A[7]));
  DIP_74377 u_B (
    .CE(nLD_B), .CLK(CLK), .D1(MEM_DQ[0]), .D2(MEM_DQ[1]), .D3(MEM_DQ[2]), .D4(MEM_DQ[3]), .D5(MEM_DQ[4]),
    .D6(MEM_DQ[5]), .D7(MEM_DQ[6]), .D8(MEM_DQ[7]), .Q1(B[0]), .Q2(B[1]), .Q3(B[2]), .Q4(B[3]), .Q5(B[4]),
    .Q6(B[5]), .Q7(B[6]), .Q8(B[7]));
  DIP_74377 MAR_L (
    .CE(nLD_MAR_L), .CLK(CLK), .D1(MEM_DQ[0]), .D2(MEM_DQ[1]), .D3(MEM_DQ[2]), .D4(MEM_DQ[3]),
    .D5(MEM_DQ[4]), .D6(MEM_DQ[5]), .D7(MEM_DQ[6]), .D8(MEM_DQ[7]), .Q1(MAR[0]), .Q2(MAR[1]), .Q3(MAR[2]),
    .Q4(MAR[3]), .Q5(MAR[4]), .Q6(MAR[5]), .Q7(MAR[6]), .Q8(MAR[7]));
  DIP_74377 MAR_H (
    .CE(nLD_MAR_H), .CLK(CLK), .D1(MEM_DQ[0]), .D2(MEM_DQ[1]), .D3(MEM_DQ[2]), .D4(MEM_DQ[3]),
    .D5(MEM_DQ[4]), .D6(MEM_DQ[5]), .D7(MEM_DQ[6]), .D8(MEM_DQ[7]), .Q1(MAR[8]), .Q2(MAR[9]), .Q3(MAR[10]),
    .Q4(MAR[11]), .Q5(MAR[12]), .Q6(MAR[13]), .Q7(MAR[14]), .Q8(MAR[15]));
  Hex_Digit_Display hex_digit_display_3 (.value(A[7:4]));  // open: dp
  Hex_Digit_Display hex_digit_display_4 (.value(B[7:4]));  // open: dp
  Hex_Digit_Display hex_digit_display_5 (.value(MAR[15:12]));  // open: dp
  Hex_Digit_Display hex_digit_display_6 (.value(A[3:0]));  // open: dp
  Hex_Digit_Display hex_digit_display_7 (.value(B[3:0]));  // open: dp
  Hex_Digit_Display hex_digit_display_8 (.value(MAR[11:8]));  // open: dp
  Hex_Digit_Display hex_digit_display_9 (.value(MAR[7:4]));  // open: dp
  Hex_Digit_Display hex_digit_display_10 (.value(MAR[3:0]));  // open: dp
endmodule

// ALU
module alu (
  input  [7:0] B,
  input  [7:0] A,
  input  nWR_MEM,
  input  nLD_PC_COND,
  output [7:0] MEM_DQ,
  output nLD_PC
);

  wire dip_7404_2_y3, dip_7408_1_y1, dip_74283_1_cout, dip_74688_1_out_18;
  wire [3:0] dip_7404_1_y1, dip_7404_1_y5, dip_74283_1_y1, dip_74283_2_y1;

  Hex_Digit_Display hex_digit_display_1 (.value(A[7:4]));  // open: dp
  Hex_Digit_Display hex_digit_display_2 (.value(A[3:0]));  // open: dp
  Hex_Digit_Display hex_digit_display_3 (.value(dip_7404_1_y5));  // open: dp
  Hex_Digit_Display hex_digit_display_4 (.value(dip_7404_1_y1));  // open: dp
  DIP_7404 dip_7404_1 (
    .A1(A[0]), .A2(A[1]), .A3(A[2]), .A4(A[3]), .A5(A[4]), .A6(A[5]), .Y1(dip_7404_1_y1[0]),
    .Y2(dip_7404_1_y1[1]), .Y3(dip_7404_1_y1[2]), .Y4(dip_7404_1_y1[3]), .Y5(dip_7404_1_y5[0]),
    .Y6(dip_7404_1_y5[1]));
  Hex_Digit_Display hex_digit_display_5 (.value(B[3:0]));  // open: dp
  Hex_Digit_Display hex_digit_display_6 (.value(B[7:4]));  // open: dp
  DIP_7404 dip_7404_2 (
    .A1(A[6]), .A2(A[7]), .A3(dip_74283_2_y1[3]), .Y1(dip_7404_1_y5[2]), .Y2(dip_7404_1_y5[3]),
    .Y3(dip_7404_2_y3));  // open: A4, A5, A6, Y4, Y5, Y6
  DIP_74283 dip_74283_1 (
    .CIN(1'b1), .A1(dip_7404_1_y1[0]), .B1(B[0]), .A2(dip_7404_1_y1[1]), .B2(B[1]), .A3(dip_7404_1_y1[2]),
    .B3(B[2]), .A4(dip_7404_1_y1[3]), .B4(B[3]), .Y1(dip_74283_1_y1[0]), .Y2(dip_74283_1_y1[1]),
    .Y3(dip_74283_1_y1[2]), .Y4(dip_74283_1_y1[3]), .COUT(dip_74283_1_cout));
  DIP_74283 dip_74283_2 (
    .CIN(dip_74283_1_cout), .A1(dip_7404_1_y5[0]), .B1(B[4]), .A2(dip_7404_1_y5[1]), .B2(B[5]),
    .A3(dip_7404_1_y5[3]), .B3(B[6]), .A4(dip_7404_1_y5[2]), .B4(B[7]), .Y1(dip_74283_2_y1[0]),
    .Y2(dip_74283_2_y1[1]), .Y3(dip_74283_2_y1[2]), .Y4(dip_74283_2_y1[3]));  // open: COUT
  DIP_74688 dip_74688_1 (
    .P0(dip_74283_1_y1[0]), .P1(dip_74283_1_y1[1]), .P2(dip_74283_1_y1[2]), .P3(dip_74283_1_y1[3]),
    .P4(dip_74283_2_y1[0]), .P5(dip_74283_2_y1[1]), .P6(dip_74283_2_y1[2]), .P7(1'b0), .R0(1'b0), .R1(1'b0),
    .R2(1'b0), .R3(1'b0), .R4(1'b0), .R5(1'b0), .R6(1'b0), .R7(dip_74283_2_y1[3]), .nOE(1'b0),
    .out_18(dip_74688_1_out_18));
  Hex_Digit_Display hex_digit_display_7 (.value(dip_74283_1_y1));  // open: dp
  Hex_Digit_Display hex_digit_display_8 (.value(dip_74283_2_y1));  // open: dp
  DIP_7408 dip_7408_1 (
    .A1(dip_7404_2_y3), .B1(dip_74688_1_out_18), .Y1(dip_7408_1_y1));  // open: A2, B2, A3, B3, A4, B4, Y2, Y3, Y4
  DIP_7432 dip_7432_1 (.A2(dip_7408_1_y1), .B2(nLD_PC_COND), .Y2(nLD_PC));  // open: A1, B1, A3, B3, A4, B4, Y1, Y3, Y4
  DIP_74541 dip_74541_1 (
    .nOE1(nWR_MEM), .nOE2(nWR_MEM), .A0(dip_74283_1_y1[0]), .A1(dip_74283_1_y1[1]), .A2(dip_74283_1_y1[2]),
    .A3(dip_74283_1_y1[3]), .A4(dip_74283_2_y1[0]), .A5(dip_74283_2_y1[1]), .A6(dip_74283_2_y1[2]),
    .A7(dip_74283_2_y1[3]), .Y0(MEM_DQ[0]), .Y1(MEM_DQ[1]), .Y2(MEM_DQ[2]), .Y3(MEM_DQ[3]), .Y4(MEM_DQ[4]),
    .Y5(MEM_DQ[5]), .Y6(MEM_DQ[6]), .Y7(MEM_DQ[7]));
endmodule

// MEM
module memory (
  input  [15:0] MAR_Q,
  input  [15:0] PC_Q,
  input  nADDR_OE,
  input  nSEL_ADD_PC_MAR,
  input  [7:0] MEM_D,
  input  nWR_MEM,
  output [15:0] MEM_ADDR,
  output [7:0] MEM_Q
);

  wire not_1_out;
  wire [7:0] ram_1_data;

  DIP_74257 dip_74257_1 (
    .A0(MAR_Q[0]), .A1(MAR_Q[1]), .A2(MAR_Q[2]), .A3(MAR_Q[3]), .B0(PC_Q[0]), .B1(PC_Q[1]), .B2(PC_Q[2]),
    .B3(PC_Q[3]), .S(nSEL_ADD_PC_MAR), .nOE(nADDR_OE), .Y0(MEM_ADDR[0]), .Y1(MEM_ADDR[1]), .Y2(MEM_ADDR[2]),
    .Y3(MEM_ADDR[3]));
  DIP_74257 dip_74257_2 (
    .A0(MAR_Q[4]), .A1(MAR_Q[5]), .A2(MAR_Q[6]), .A3(MAR_Q[7]), .B0(PC_Q[4]), .B1(PC_Q[5]), .B2(PC_Q[6]),
    .B3(PC_Q[7]), .S(nSEL_ADD_PC_MAR), .nOE(nADDR_OE), .Y0(MEM_ADDR[4]), .Y1(MEM_ADDR[5]), .Y2(MEM_ADDR[6]),
    .Y3(MEM_ADDR[7]));
  DIP_74257 dip_74257_3 (
    .A0(MAR_Q[8]), .A1(MAR_Q[9]), .A2(MAR_Q[10]), .A3(MAR_Q[11]), .B0(PC_Q[8]), .B1(PC_Q[9]), .B2(PC_Q[10]),
    .B3(PC_Q[11]), .S(nSEL_ADD_PC_MAR), .nOE(nADDR_OE), .Y0(MEM_ADDR[8]), .Y1(MEM_ADDR[9]),
    .Y2(MEM_ADDR[10]), .Y3(MEM_ADDR[11]));
  DIP_74257 dip_74257_4 (
    .A0(MAR_Q[12]), .A1(MAR_Q[13]), .A2(MAR_Q[14]), .A3(MAR_Q[15]), .B0(PC_Q[12]), .B1(PC_Q[13]),
    .B2(PC_Q[14]), .B3(PC_Q[15]), .S(nSEL_ADD_PC_MAR), .nOE(nADDR_OE), .Y0(MEM_ADDR[12]), .Y1(MEM_ADDR[13]),
    .Y2(MEM_ADDR[14]), .Y3(MEM_ADDR[15]));
  assign MEM_Q = nWR_MEM ? ram_1_data : 8'bz;  // Controlled_Buffer controlled_buffer_1
  RAM #(.addrWidth(16), .bus("asynch")) ram_1 (
    .addr(MEM_ADDR), .data(ram_1_data), .sel(1'b1), .ld(nWR_MEM), .clr(1'b0));
  assign ram_1_data = not_1_out ? MEM_D : 8'bz;  // Controlled_Buffer controlled_buffer_2
  not not_1 (not_1_out, nWR_MEM);
endmodule
